// Logisim project traffic-light-system.circ as structural Verilog: 3 circuits, main circuit main
module main (
  input  in_1,
  input  in_2
);

  wire [3:0] n4_bit_counter_1_out_3;

  _4_bit_counter u_4_bit_counter_1 (
    .Power(in_1), .Zero(in_2), .out_3(n4_bit_counter_1_out_3[0]), .out_4(n4_bit_counter_1_out_3[1]),
    .out_5(n4_bit_counter_1_out_3[2]), .out_6(n4_bit_counter_1_out_3[3]));
  Hex_Digit_Display hex_digit_display_1 (.value(n4_bit_counter_1_out_3));  // open: dp
endmodule

module _4_bit_counter (
  input  Power,
  input  Zero,
  output out_3,
  output out_4,
  output out_5,
  output out_6
);

  wire and_1_out, and_2_out, clock_1_out, not_1_out;

  Clock clock_1 (.out(clock_1_out));
  not not_1 (not_1_out, clock_1_out);
  J_K_Flip_Flop j_k_ff_1 (.J(Power), .clk(not_1_out), .K(Power), .Q(out_3), .reset(Zero));  // open: Qn, preset, en
  and and_1 (and_1_out, out_3, out_4);
  J_K_Flip_Flop j_k_ff_2 (
    .J(out_3), .clk(not_1_out), .K(out_3), .Q(out_4), .en(Power), .reset(Zero));  // open: Qn, preset
  J_K_Flip_Flop j_k_ff_3 (
    .J(and_1_out), .clk(not_1_out), .K(and_1_out), .Q(out_5), .en(Power), .reset(Zero));  // open: Qn, preset
  and and_2 (and_2_out, out_3, out_4, out_5);
  J_K_Flip_Flop j_k_ff_4 (
    .J(and_2_out), .clk(not_1_out), .K(and_2_out), .Q(out_6), .en(Power), .reset(Zero));  // open: Qn, preset

  // Notes on the sheet:
  //   Clock
endmodule

module controller (
  input  [3:0] in_1,
  output [1:0] South
);

  wire not_1_out, not_2_out, not_3_out, not_4_out, or_1_out;

  not not_1 (not_1_out, in_1[3]);
  not not_2 (not_2_out, in_1[2]);
  not not_3 (not_3_out, in_1[1]);
  not not_4 (not_4_out, in_1[0]);
  and and_1 (South[0], in_1[0], in_1[1], not_1_out, not_2_out);
  and and_2 (South[1], not_1_out, not_2_out, or_1_out);
  or or_1 (or_1_out, not_3_out, not_4_out);
endmodule
